# Fritzing sketch snake_schematic (saved by Fritzing 1.0.3b)
breadboards: 1

parts:
  Part1 = Thumb Joystick
  Mod1 = ESP32-TTGO-T-DISPLAY
  R1 = Rotary Potentiometer (Small) [maximum_resistance=10kΩ knob_status=50% power=0.5W package=THT]
  S1 = Momentary Switch [package=ksa_sealed_tac_switch]

nets:
  N1: Part1.GND, Mod1.G-1, Mod1.G-2, Mod1.G-10, Mod1.G-11, Mod1.G-14, R1.leg2
  N2: Part1.HORZ, Mod1.39
  N3: Part1.VERT, Mod1.32
  N4: Part1.VCC, Mod1.3V, R1.leg1, S1.4
  N5: Mod1.27, S1.2
  N6: Mod1.38, R1.wiper

custom parts:
  ESP32-TTGO-T-DISPLAY: LILYGO TTGO T-Display GD32VF103CBT6 Main Chip ST7789 1.14 Inch IPS 240x135 Resolution Minimalist Development Board.
